# Fritzing sketch voting_booth (saved by Fritzing 0.9.3b)

parts:
  BAT1 = BC9VPC [package=bc9vpc]
  R2 = Resistor [tolerance=±5% resistance=5.1k package="0603 [SMD]"]
  U3 = Nokia 6100 Color LCD [part_number=NEXTION package=nokia6100_lcd]
  R3 = Resistor [tolerance=±5% resistance=3.9k package="0603 [SMD]"]
  LED1 = LED - 3mm [color="Red (633nm)" package="3 mm [THT]"]
  R4 = Resistor [tolerance=±5% resistance=220 package="0603 [SMD]"]  # not connected
  Part1 = SparkFun ESP8266 Thing
  U4 = PCA9306 [package=psop-8]
  R5 = Resistor [tolerance=±5% resistance=1k package=THT]
  R6 = Resistor [tolerance=±5% resistance=2k package=THT]

nets:
  N1: BAT1.V+, R3.Pin_0
  N2: BAT1.V-, R2.Pin_1
  N3: U3.VDIGITAL, R3.Pin_1, R5.Pin_0
  N4: U3.RESET, U4.SCL2
  N5: U3.DIO, U4.SDA2
  N6: U3.CS, LED1.anode, R6.Pin_1
  N7: Part1.VCC, R5.Pin_1, R6.Pin_0
  N8: Part1.U0TXO, U4.SCL1
  N9: Part1.U0RXI, U4.SDA1

notes:
  NEXTION SCREEN
  VOLTAGE DIVIDER->OUT 5V
  PCA9306 LEVEL SHIFTER
  TX
  RX
  INDICATOR LED
  MCU RX -> SCREEN TX
  MCU TX -> SCREEN RX
  VOLTAGE DIVIDER ->OUT 3.3V
  ESP8266
  9V 700mAh Rechargeable
